// Logisim project 4-bit full adder.circ as structural Verilog: 2 circuits, main circuit main
module main (
  input  in_1,
  input  in_2,
  input  in_3,
  output out_4,
  output out_5
);

  wire and_1_out, and_2_out, xor_1_out;

  xor xor_1 (xor_1_out, in_1, in_2);
  and and_1 (and_1_out, in_1, in_2);
  xor xor_2 (out_4, xor_1_out, in_3);
  and and_2 (and_2_out, xor_1_out, in_3);
  or or_1 (out_5, and_2_out, and_1_out);
endmodule

module _4_bit_full_adder (
  input  in_1,
  input  in_2,
  input  C_in,
  input  in_4,
  input  in_5,
  input  in_6,
  input  in_7,
  input  in_8,
  input  in_9
);

  wire main_1_out_5, main_2_out_5, main_3_out_5;
  wire [3:0] main_1_out_4;

  main main_1 (.in_1(in_1), .in_2(in_2), .in_3(C_in), .out_4(main_1_out_4[0]), .out_5(main_1_out_5));
  main main_2 (.in_1(main_1_out_5), .in_2(in_4), .in_3(in_5), .out_4(main_1_out_4[1]), .out_5(main_2_out_5));
  main main_3 (.in_1(main_2_out_5), .in_2(in_6), .in_3(in_7), .out_4(main_1_out_4[2]), .out_5(main_3_out_5));
  main main_4 (.in_1(main_3_out_5), .in_2(in_8), .in_3(in_9), .out_4(main_1_out_4[3]));  // open: out_5
  Hex_Digit_Display hex_digit_display_1 (.value(main_1_out_4));  // open: dp
endmodule
