// Logisim project Lab1_2.circ as structural Verilog: 1 circuit, main circuit main
module main (
  input  A,
  input  x,
  input  y,
  input  B,
  input  C,
  input  z,
  input  w,
  input  x_2,
  input  in_9,
  input  z_2,
  input  x_3,
  input  y_2,
  output out_13,
  output out_14,
  output out_15,
  output out_16
);

  wire AB_out, ABC_2_out, ABC_out, and_2_out, or_4_out, wz_2_out, wz_out, x_y_2_out, x_y_out, xy_out,
       xyz_out, xz_out;

  or x_y (x_y_out, x_3, y_2);
  or x_y_2 (x_y_2_out, x_3, y_2);
  and ABC (ABC_out, A, B, C);
  and AB (AB_out, A, C);
  and ABC_2 (ABC_2_out, A, B, C);
  and xyz (xyz_out, x_2, z_2, in_9);
  and xz (xz_out, x_2, z_2);
  or or_1 (out_15, xyz_out, xz_out);
  and and_1 (out_16, x_y_out, x_y_2_out);
  or or_2 (out_14, ABC_out, AB_out, ABC_2_out);
  and xy (xy_out, x, x, y);
  and wz (wz_out, w, z);
  and wz_2 (wz_2_out, z, w);
  and and_2 (and_2_out, x, or_4_out);
  or or_3 (out_13, xy_out, and_2_out);
  or or_4 (or_4_out, wz_out, wz_2_out);

  // Notes on the sheet:
  //   y
  //   (x+y)(x+y)
  //   xyz+xz
  //   ABC + AB +ABC
  //   Hà Duy Tân
  //   x(wz+wz)
  //   xy+x(wz+wz)
  //   wz+wz
endmodule
