// Logisim project Lab1_3.circ as structural Verilog
module mux_2_1 (
  input  in_1,
  input  in_2,
  input  in_3,
  output out_4
);

  wire and_1_out, and_2_out, not_1_out;

  and and_1 (and_1_out, in_1, not_1_out);
  not not_1 (not_1_out, in_3);
  and and_2 (and_2_out, in_2, in_3);
  or or_1 (out_4, and_1_out, and_2_out);

  // Notes on the sheet:
  //   Hà Duy Tân
endmodule

module mux_4_1 (
  input  In_00,
  input  In_01,
  input  In_10,
  input  In_11,
  input  sel_0,
  input  sel_1,
  output out_7
);

  wire mux_2_1_1_out_4, mux_2_1_2_out_4;

  mux_2_1 mux_2_1_1 (.in_1(In_00), .in_2(In_01), .in_3(sel_1), .out_4(mux_2_1_1_out_4));
  mux_2_1 mux_2_1_2 (.in_1(In_10), .in_2(In_11), .in_3(sel_1), .out_4(mux_2_1_2_out_4));
  mux_2_1 mux_2_1_3 (.in_1(mux_2_1_1_out_4), .in_2(mux_2_1_2_out_4), .in_3(sel_0), .out_4(out_7));

  // Notes on the sheet:
  //   Hà Duy Tân
endmodule

module mux_8_1 (
  input  In_0,
  input  In_1,
  input  In_2,
  input  In_3,
  input  In4,
  input  In_5,
  input  In_6,
  input  In_7,
  input  S2,
  input  S0,
  input  S1,
  output out_12
);

  wire mux_4_1_1_out_7, mux_4_1_2_out_7;

  mux_4_1 mux_4_1_1 (
    .In_00(In_0), .In_01(In_1), .In_10(In_2), .In_11(In_3), .sel_0(S0), .sel_1(S1), .out_7(mux_4_1_1_out_7));
  mux_4_1 mux_4_1_2 (
    .In_00(In4), .In_01(In_5), .In_10(In_6), .In_11(In_7), .sel_0(S0), .sel_1(S1), .out_7(mux_4_1_2_out_7));
  mux_2_1 mux_2_1_1 (.in_1(mux_4_1_1_out_7), .in_2(mux_4_1_2_out_7), .in_3(S2), .out_4(out_12));

  // Notes on the sheet:
  //   Hà Duy Tân
endmodule
