// Logisim project MyFirstCircuite.circ as structural Verilog: 1 circuit, main circuit main
module main (
  input  A,
  input  in_2,
  output X
);

  wire and_1_out, and_2_out, not_1_out, not_2_out;

  not not_1 (not_1_out, A);
  not not_2 (not_2_out, in_2);
  and and_1 (and_1_out, not_1_out, in_2);
  and and_2 (and_2_out, A, not_2_out);
  or or_1 (X, and_1_out, and_2_out);

  // Notes on the sheet:
  //   B
  //   Hà Duy Tân
endmodule
